// Logisim project Exemplo_1201.circ as structural Verilog: 3 circuits, main circuit main
module main (
  input  Add,
  input  [3:0] Input,
  input  R_W,
  input  Clear,
  output [3:0] Output
);

  wire clock_1_out;

  Clock clock_1 (.out(clock_1_out));
  M1X4 m1x4_1 (.Add(Add), .Clk(clock_1_out), .R_W(R_W), .in_4(Clear), .Input(Input), .Output(Output));
endmodule

module M1X1 (
  input  Address,
  input  Clock,
  input  R_W,
  input  Input,
  input  CLR,
  output Output
);

  wire and_1_out, and_2_out, and_3_out, controlled_buffer_1_out, j_k_ff_1_q, not_1_out;

  assign controlled_buffer_1_out = R_W ? Input : 1'bz;  // Controlled_Buffer controlled_buffer_1
  and and_1 (and_1_out, Address, Clock, R_W);
  not not_1 (not_1_out, controlled_buffer_1_out);
  J_K_Flip_Flop j_k_ff_1 (
    .J(controlled_buffer_1_out), .clk(and_1_out), .K(not_1_out), .Q(j_k_ff_1_q), .reset(CLR));  // open: Qn, preset
  assign Output = and_3_out ? and_2_out : 1'bz;  // Controlled_Buffer controlled_buffer_2
  and and_2 (and_2_out, Address, j_k_ff_1_q);
  and and_3 (and_3_out, ~Clock, Address);  // AND_Gate
endmodule

module M1X4 (
  input  Add,
  input  Clk,
  input  R_W,
  input  in_4,
  input  [3:0] Input,
  output [3:0] Output
);

  M1X1 m1x1_1 (.Address(Add), .Clock(Clk), .R_W(R_W), .CLR(in_4), .Output(Output[3]), .Input(Input[3]));
  M1X1 m1x1_2 (.Address(Add), .Clock(Clk), .R_W(R_W), .CLR(in_4), .Output(Output[2]), .Input(Input[2]));
  M1X1 m1x1_3 (.Address(Add), .Clock(Clk), .R_W(R_W), .CLR(in_4), .Output(Output[1]), .Input(Input[1]));
  M1X1 m1x1_4 (.Address(Add), .Clock(Clk), .R_W(R_W), .CLR(in_4), .Output(Output[0]), .Input(Input[0]));
endmodule
