// Logisim project Exemplo_1202.circ as structural Verilog: 3 circuits, main circuit main
module main (
  input  Add,
  input  R_W,
  input  Clear,
  input  [3:0] Input,
  output [3:0] Output
);

  wire clock_1_out;

  Clock clock_1 (.out(clock_1_out));
  M1X2 m1x2_1 (.Add(Add), .CLK(clock_1_out), .R_W(R_W), .Clear(Clear), .Input(Input[3:2]), .Output(Output[3:2]));
  M1X2 m1x2_2 (.Add(Add), .CLK(clock_1_out), .R_W(R_W), .Clear(Clear), .Input(Input[1:0]), .Output(Output[1:0]));
endmodule

module M1X1 (
  input  Address,
  input  Clock,
  input  R_W,
  input  Input,
  input  CLR,
  output Output
);

  wire and_1_out, and_2_out, and_3_out, controlled_buffer_1_out, j_k_ff_1_q, not_1_out;

  assign controlled_buffer_1_out = R_W ? Input : 1'bz;  // Controlled_Buffer controlled_buffer_1
  and and_1 (and_1_out, Address, Clock, R_W);
  not not_1 (not_1_out, controlled_buffer_1_out);
  J_K_Flip_Flop j_k_ff_1 (
    .J(controlled_buffer_1_out), .clk(and_1_out), .K(not_1_out), .Q(j_k_ff_1_q), .reset(CLR));  // open: Qn, preset
  and and_2 (and_2_out, Address, j_k_ff_1_q);
  assign Output = and_3_out ? and_2_out : 1'bz;  // Controlled_Buffer controlled_buffer_2
  and and_3 (and_3_out, ~Clock, Address);  // AND_Gate
endmodule

module M1X2 (
  input  Add,
  input  CLK,
  input  R_W,
  input  Clear,
  input  [1:0] Input,
  output [1:0] Output
);

  M1X1 m1x1_1 (.Address(Add), .Clock(CLK), .R_W(R_W), .CLR(Clear), .Output(Output[1]), .Input(Input[1]));
  M1X1 m1x1_2 (.Address(Add), .Clock(CLK), .R_W(R_W), .CLR(Clear), .Output(Output[0]), .Input(Input[0]));
endmodule
