// Logisim project Exemplo_1207.circ as structural Verilog: 7 circuits, main circuit main
// M1X16
module main (
  input  [1:0] Add,
  input  R_W,
  input  Clear,
  input  [15:0] Input,
  output [15:0] Output
);

  wire clock_1_out, demultiplexer_1_out0, demultiplexer_1_out1, demultiplexer_1_out2, demultiplexer_1_out3;
  wire [15:0] n1x16_1_output, n1x16_2_output, n1x16_4_output;

  Clock clock_1 (.out(clock_1_out));
  Demultiplexer #(.select(2), .enable("false")) demultiplexer_1 (
    .out0(demultiplexer_1_out0), .out1(demultiplexer_1_out1), .out2(demultiplexer_1_out2),
    .out3(demultiplexer_1_out3), .in(1'b1), .sel(Add));
  _1X16 u_1x16_1 (
    .Add(demultiplexer_1_out3), .clk(clock_1_out), .R_W(R_W), .Clear(Clear), .Output(n1x16_1_output),
    .Input(Input));
  _1X16 u_1x16_2 (
    .Add(demultiplexer_1_out2), .clk(clock_1_out), .R_W(R_W), .Clear(Clear), .Output(n1x16_2_output),
    .Input(Input));
  _1X16 u_1x16_3 (
    .Add(demultiplexer_1_out1), .clk(clock_1_out), .R_W(R_W), .Clear(Clear), .Output(n1x16_2_output),
    .Input(Input));
  _1X16 u_1x16_4 (
    .Add(demultiplexer_1_out0), .clk(clock_1_out), .R_W(R_W), .Clear(Clear), .Output(n1x16_4_output),
    .Input(Input));
  Multiplexer #(.select(2), .width(16), .enable("false")) multiplexer_1 (
    .in0(n1x16_4_output), .in1(n1x16_2_output), .in2(n1x16_2_output), .in3(n1x16_1_output), .out(Output),
    .sel(Add));
endmodule

module M1X1 (
  input  Address,
  input  Clock,
  input  R_W,
  input  Input,
  input  CLR,
  output Output
);

  wire and_1_out, and_2_out, and_3_out, controlled_buffer_1_out, j_k_ff_1_q, not_1_out;

  assign controlled_buffer_1_out = R_W ? Input : 1'bz;  // Controlled_Buffer controlled_buffer_1
  and and_1 (and_1_out, Address, Clock, R_W);
  not not_1 (not_1_out, controlled_buffer_1_out);
  J_K_Flip_Flop j_k_ff_1 (
    .J(controlled_buffer_1_out), .clk(and_1_out), .K(not_1_out), .Q(j_k_ff_1_q), .reset(CLR));  // open: Qn, preset
  and and_2 (and_2_out, Address, j_k_ff_1_q);
  assign Output = and_3_out ? and_2_out : 1'bz;  // Controlled_Buffer controlled_buffer_2
  and and_3 (and_3_out, ~Clock, Address);  // AND_Gate
endmodule

module M1X2 (
  input  Add,
  input  CLK,
  input  R_W,
  input  Clear,
  input  [1:0] Input,
  output [1:0] Output
);

  M1X1 m1x1_1 (.Address(Add), .Clock(CLK), .R_W(R_W), .CLR(Clear), .Output(Output[1]), .Input(Input[1]));
  M1X1 m1x1_2 (.Address(Add), .Clock(CLK), .R_W(R_W), .CLR(Clear), .Output(Output[0]), .Input(Input[0]));
endmodule

module M1X8 (
  input  Add,
  input  Clk,
  input  R_W,
  input  Clear,
  input  [7:0] Input,
  output [7:0] Output
);

  _1X4 u_1x4_1 (.Add(Add), .Clk(Clk), .R_W(R_W), .Clear(Clear), .Input(Input[7:4]), .Output(Output[7:4]));
  _1X4 u_1x4_2 (.Add(Add), .Clk(Clk), .R_W(R_W), .Clear(Clear), .Input(Input[3:0]), .Output(Output[3:0]));
endmodule

module _1X4 (
  input  Add,
  input  Clk,
  input  R_W,
  input  Clear,
  input  [3:0] Input,
  output [3:0] Output
);

  M1X2 m1x2_1 (.Add(Add), .CLK(Clk), .R_W(R_W), .Clear(Clear), .Input(Input[3:2]), .Output(Output[3:2]));
  M1X2 m1x2_2 (.Add(Add), .CLK(Clk), .R_W(R_W), .Clear(Clear), .Input(Input[1:0]), .Output(Output[1:0]));
endmodule

// 4X8
module M4X8 (
  input  [1:0] Add,
  input  Clk,
  input  R_W,
  input  Clear,
  input  [7:0] Input,
  output [7:0] Output
);

  wire demultiplexer_1_out0, demultiplexer_1_out1, demultiplexer_1_out2, demultiplexer_1_out3;
  wire [7:0] m1x8_1_output, m1x8_2_output, m1x8_3_output, m1x8_4_output;

  Demultiplexer #(.select(2), .enable("false")) demultiplexer_1 (
    .out0(demultiplexer_1_out0), .out1(demultiplexer_1_out1), .out2(demultiplexer_1_out2),
    .out3(demultiplexer_1_out3), .in(1'b1), .sel(Add));
  M1X8 m1x8_1 (.Add(demultiplexer_1_out3), .Clk(Clk), .R_W(R_W), .Clear(Clear), .Input(Input), .Output(m1x8_1_output));
  M1X8 m1x8_2 (.Add(demultiplexer_1_out2), .Clk(Clk), .R_W(R_W), .Clear(Clear), .Input(Input), .Output(m1x8_2_output));
  M1X8 m1x8_3 (.Add(demultiplexer_1_out1), .Clk(Clk), .R_W(R_W), .Clear(Clear), .Input(Input), .Output(m1x8_3_output));
  M1X8 m1x8_4 (.Add(demultiplexer_1_out0), .Clk(Clk), .R_W(R_W), .Clear(Clear), .Input(Input), .Output(m1x8_4_output));
  Multiplexer #(.select(2), .width(8), .enable("false")) multiplexer_1 (
    .in0(m1x8_4_output), .in1(m1x8_3_output), .in2(m1x8_2_output), .in3(m1x8_1_output), .out(Output),
    .sel(Add));
endmodule

module _1X16 (
  input  Add,
  input  clk,
  input  R_W,
  input  Clear,
  input  [15:0] Input,
  output [15:0] Output
);

  M1X8 m1x8_1 (.Add(Add), .Clk(clk), .R_W(R_W), .Clear(Clear), .Input(Input[15:8]), .Output(Output[15:8]));
  M1X8 m1x8_2 (.Add(Add), .Clk(clk), .R_W(R_W), .Clear(Clear), .Input(Input[7:0]), .Output(Output[7:0]));
endmodule
